# Fritzing sketch SoilSchematic (saved by Fritzing 0.9.3b)
perfboards: 1

parts:
  Xenon1 = Particle Xenon
  SolarPanel = Screw terminal - 2 pins [package=THT]
  IC1 = Voltage Regulator [package=78xxl]
  BME280-I2C = Screw terminal - 2 pins [package=THT]
  BME280-Power = Screw terminal - 2 pins [package=THT]
  C1 = Electrolytic Capacitor [capacitance=10µF package="100 mil [THT, electrolytic]"]
  C2 = Electrolytic Capacitor [capacitance=10µF package="100 mil [THT, electrolytic]"]
  part = BMP280
  Part1 = INA219 High Side DC Current Sensor Breakout [part_number=904]
  1N5819 = Schottky Diode [part_number=1N5817 package="Melf DO-213 AB [SMD]"]
  D1 = SOLAR-IXYS [package=solarbit-12x1]
  J1 = male pin header, 3 pins [form="♂ (male)"]
  SW1 = DIP SWITCH [package=dipswitch-02]
  Part2 = Soil Moisture Sensor

nets:
  VCC: Xenon1.3.3V, BME280-Power.pin1, part.VIN, Part1.VCC, J1.pin2, Part2.VCC
  GND: Xenon1.GND, SolarPanel.pin2, Part1.GND, D1.A, SW1.1, SW1.2
  N1: Xenon1.A2, J1.pin3, Part2.SIG
  N2: Xenon1.SDA, BME280-I2C.pin2, part.SDA, Part1.SDA
  N3: Xenon1.SCL, BME280-I2C.pin1, part.SCL, Part1.SCL
  N4: Xenon1.D4, SW1.4
  N5: Xenon1.D5, SW1.3
  N6: Xenon1.VUSB, IC1.OUT, C1.+
  N7: SolarPanel.pin1, 1N5819.anode, D1.C
  N8: IC1.GND, C1.-, C2.-
  N9: IC1.IN, C2.+, Part1.VIN-
  N10: BME280-Power.pin2, part.GND
  N11: Part1.VIN+, 1N5819.cathode
  N12: J1.pin1, Part2.GND

custom parts:
  Particle Xenon: The Boron LTE is a powerful LTE CAT-M1 enabled development kit that can act as either a standalone cellular device or LTE enabled gateway, repeater, or endpoint for a Particle Mesh networks. Equipped with the Nordic nRF52840 and u-blox SARA 410 processors, the Boron has built-in battery charging circuitry which makes it easier to connect a Li-Po battery and 20 mixed signal GPIOs to interface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
  BMP280: Temperature Humidity Barometric presure Sensor, I2C
  INA219 High Side DC Current Sensor Breakout: This breakout board will solve all your power-monitoring problems. Instead of struggling with two multimeters, you can just use the handy INA219B chip on this breakout to both measure both the high side voltage and DC current draw over I2C with 1% precision. Most current-measuring devices such as our current panel meter are only good for low side measuring. That means that unless you want to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
